// Logisim project control.circ as structural Verilog: 1 circuit, main circuit main
module main (
  input  start,
  input  eq1,
  input  clock,
  input  eq0,
  input  eq,
  input  lt,
  output Sa,
  output Sb,
  output Sc,
  output La,
  output Lb,
  output Shift,
  output Lcount,
  output Sr1,
  output Sr2,
  output Scr,
  output Cr,
  output [2:0] state
);

  wire and_3_out, and_4_out, and_6_out, and_7_out, and_8_out, and_9_out, and_10_out, and_11_out, and_12_out,
       and_13_out, and_14_out, and_15_out, and_16_out, and_17_out, and_18_out, and_19_out, and_20_out,
       and_21_out, and_22_out, and_23_out, and_24_out, and_25_out, and_26_out, and_27_out, and_28_out,
       and_29_out, and_30_out, and_31_out, and_32_out, and_35_out, and_37_out, and_38_out, and_39_out,
       and_40_out, and_41_out, not_1_out, not_2_out, not_3_out, not_4_out, not_5_out, not_6_out, not_7_out,
       not_8_out, not_9_out, not_10_out, not_11_out, not_12_out, not_13_out, not_14_out, not_15_out,
       not_16_out, not_17_out, not_18_out, not_19_out, not_20_out, not_21_out, not_22_out, not_23_out,
       not_24_out, not_25_out, not_26_out, not_27_out, not_28_out, not_29_out, not_30_out, not_31_out,
       not_32_out, not_33_out, not_34_out, not_35_out, or_2_out, or_3_out, or_4_out, or_10_out;
  wire [2:0] or_11_out;

  Register #(.width(3)) register_1 (.D(or_11_out), .en(1'b1), .Q(state), .clk(clock));  // open: clr
  not not_1 (not_1_out, state[2]);
  not not_2 (not_2_out, state[2]);
  not not_3 (not_3_out, state[1]);
  not not_4 (not_4_out, state[2]);
  not not_5 (not_5_out, state[0]);
  not not_6 (not_6_out, eq0);
  not not_7 (not_7_out, state[2]);
  and and_1 (Sa, state[2], state[0]);
  and and_2 (Sb, state[1], state[0]);
  not not_8 (not_8_out, state[1]);
  and and_3 (and_3_out, state[1], state[0]);
  and and_4 (and_4_out, state[2], state[0]);
  not not_9 (not_9_out, state[2]);
  not not_10 (not_10_out, state[1]);
  not not_11 (not_11_out, state[1]);
  not not_12 (not_12_out, state[1]);
  and and_5 (Lcount, state[2], state[0]);
  not not_13 (not_13_out, state[2]);
  not not_14 (not_14_out, state[1]);
  not not_15 (not_15_out, state[2]);
  not not_16 (not_16_out, state[1]);
  and and_6 (and_6_out, not_1_out, state[1]);
  not not_17 (not_17_out, eq1);
  and and_7 (and_7_out, not_2_out, state[1]);
  not not_18 (not_18_out, lt);
  and and_8 (and_8_out, state[2], not_3_out);
  not not_19 (not_19_out, state[0]);
  not not_20 (not_20_out, state[1]);
  and and_9 (and_9_out, not_4_out, state[1]);
  and and_10 (and_10_out, not_5_out, not_6_out);
  not not_21 (not_21_out, state[2]);
  not not_22 (not_22_out, state[0]);
  not not_23 (not_23_out, lt);
  not not_24 (not_24_out, state[1]);
  not not_25 (not_25_out, state[0]);
  and and_11 (and_11_out, not_7_out, state[1]);
  not not_26 (not_26_out, state[0]);
  not not_27 (not_27_out, eq0);
  not not_28 (not_28_out, eq);
  and and_12 (and_12_out, state[2], not_8_out);
  not not_29 (not_29_out, state[0]);
  or or_1 (La, and_3_out, and_4_out);
  and and_13 (and_13_out, not_9_out, not_10_out);
  and and_14 (and_14_out, state[2], not_11_out);
  not not_30 (not_30_out, state[0]);
  and and_15 (and_15_out, state[2], not_12_out);
  not not_31 (not_31_out, state[0]);
  and and_16 (and_16_out, not_13_out, not_14_out);
  not not_32 (not_32_out, state[0]);
  and and_17 (and_17_out, not_15_out, not_16_out);
  not not_33 (not_33_out, state[0]);
  and and_18 (and_18_out, and_6_out, not_17_out);
  or or_2 (or_2_out, and_18_out, and_19_out);
  and and_19 (and_19_out, and_7_out, not_18_out);
  and and_20 (and_20_out, state[1], state[0]);
  or or_3 (or_3_out, and_20_out, and_21_out);
  and and_21 (and_21_out, and_8_out, not_19_out);
  and and_22 (and_22_out, not_20_out, state[0]);
  or or_4 (or_4_out, and_22_out, and_23_out);
  and and_23 (and_23_out, and_9_out, and_10_out);
  and and_24 (and_24_out, not_21_out, state[1]);
  and and_25 (and_25_out, and_24_out, and_26_out);
  and and_26 (and_26_out, not_22_out, not_23_out);
  and and_27 (and_27_out, not_24_out, not_25_out);
  and and_28 (and_28_out, and_27_out, start);
  and and_29 (and_29_out, and_11_out, not_26_out);
  and and_30 (and_30_out, and_29_out, and_31_out);
  and and_31 (and_31_out, not_27_out, not_28_out);
  and and_32 (and_32_out, state[2], not_34_out);
  not not_34 (not_34_out, state[1]);
  not not_35 (not_35_out, state[0]);
  and and_33 (Sc, and_12_out, not_29_out);
  and and_34 (Cr, and_13_out, state[0]);
  or or_5 (Lb, Cr, and_35_out);
  and and_35 (and_35_out, and_14_out, not_30_out);
  and and_36 (Shift, and_15_out, not_31_out);
  and and_37 (and_37_out, and_16_out, not_32_out);
  or or_6 (Sr1, and_37_out, and_38_out);
  and and_38 (and_38_out, state[2], state[1]);
  and and_39 (and_39_out, and_17_out, not_33_out);
  or or_7 (Sr2, and_39_out, and_40_out);
  and and_40 (and_40_out, state[2], state[1]);
  or or_8 (or_11_out[2], or_2_out, or_3_out);
  or or_9 (or_11_out[1], or_4_out, and_25_out);
  or or_10 (or_10_out, and_28_out, and_30_out);
  and and_41 (and_41_out, and_32_out, not_35_out);
  or or_11 (or_11_out[0], or_10_out, and_41_out);

  assign Scr = Lcount;

  // Notes on the sheet:
  //   N2
  //   N1
  //   N0
endmodule
