// Logisim project datapath.circ as structural Verilog: 1 circuit, main circuit main
module main (
  input  [31:0] Multiplicand,
  input  Sr1,
  input  Sb,
  input  La,
  input  Sr2,
  input  Sa,
  input  [31:0] Multiplier,
  input  Lb,
  input  Sc,
  input  Cr,
  input  Scr,
  input  Lcount,
  input  clock,
  input  Shift,
  output [31:0] Hi,
  output [31:0] Lo,
  output eq1,
  output eq0,
  output eq,
  output lt
);

  wire [5:0] adder_2_out, multiplexer_1_out, register_1_q;
  wire [31:0] adder_1_out, multiplexer_2_out, multiplexer_3_out, multiplexer_4_out, register_2_q,
       register_3_q, shifter_1_out_2, shifter_2_out;
  wire [31:31] shifter_1_out;

  Multiplexer #(.width(6), .enable("false")) multiplexer_1 (
    .in0({6{1'b0}}), .in1(adder_2_out), .out(multiplexer_1_out), .sel(Scr));
  Register #(.width(6)) register_1 (.D(multiplexer_1_out), .en(Lcount), .Q(register_1_q), .clk(clock), .clr(Cr));
  Multiplexer #(.width(32), .enable("false")) multiplexer_2 (
    .in0(register_3_q), .in1(shifter_2_out), .out(multiplexer_2_out), .sel(Sa));
  Adder #(.width(32)) adder_1 (.a(Multiplicand), .b(multiplexer_2_out), .out(adder_1_out), .cin(1'b0));  // open: cout
  Multiplexer #(.width(32), .enable("false")) multiplexer_3 (
    .in0(Multiplier), .in1(shifter_1_out_2), .out(multiplexer_3_out), .sel(Sc));
  Adder #(.width(6)) adder_2 (.a(register_1_q), .b(6'b000001), .out(adder_2_out));  // open: cin, cout
  Comparator #(.width(6), .mode("unsigned")) comparator_1 (
    .a(adder_2_out), .b(6'b100000), .eq(eq), .lt(lt));  // open: gt
  Multiplexer #(.width(32), .enable("false")) multiplexer_4 (
    .in0(multiplexer_2_out), .in1(adder_1_out), .out(multiplexer_4_out), .sel(Sb));
  Register #(.width(32)) register_2 (.D(multiplexer_3_out), .en(Lb), .Q(register_2_q), .clk(clock));  // open: clr
  Register #(.width(32)) register_3 (.D(multiplexer_4_out), .en(La), .Q(register_3_q), .clk(clock), .clr(Cr));
  Shifter #(.width(32), .shift("lr")) shifter_1 (
    .in(register_2_q), .\dist (5'b00001), .out({shifter_1_out[31], shifter_1_out_2[30:0]}));
  Shifter #(.width(32), .shift("lr")) shifter_2 (.in(register_3_q), .\dist (5'b00001), .out(shifter_2_out));
  Multiplexer #(.enable("false")) multiplexer_5 (
    .in0(shifter_1_out[31]), .in1(register_3_q[0]), .out(shifter_1_out_2[31]), .sel(Shift));
  Comparator #(.width(1)) comparator_2 (.a(register_2_q[0]), .b(1'b1), .eq(eq1));  // open: gt, lt
  Comparator #(.width(1)) comparator_3 (.a(register_2_q[0]), .b(1'b0), .eq(eq0));  // open: gt, lt
  Multiplexer #(.width(32), .enable("false")) multiplexer_6 (
    .in0({32{1'b0}}), .in1(shifter_2_out), .out(Hi), .sel(Sr1));
  Multiplexer #(.width(32), .enable("false")) multiplexer_7 (
    .in0({32{1'b0}}), .in1({shifter_1_out[31], shifter_1_out_2[30:0]}), .out(Lo), .sel(Sr2));
endmodule
