// Logisim project mult32.circ as structural Verilog: 1 circuit, main circuit main
module main (
  input  [31:0] multiplicand,
  input  [31:0] multiplier,
  output [31:0] Hi,
  output [31:0] Lo,
  output [2:0] state
);

  wire clock_1_out, main_1_cr, main_1_la, main_1_lb, main_1_lcount, main_1_sa, main_1_sb, main_1_sc,
       main_1_scr, main_1_shift, main_1_sr1, main_1_sr2, main_2_eq, main_2_eq0, main_2_eq1, main_2_lt,
       start_out;

  Button start (.out(start_out));
  Clock clock_1 (.out(clock_1_out));
  control_main main_1 (
    .start(start_out), .eq1(main_2_eq1), .eq0(main_2_eq0), .eq(main_2_eq), .lt(main_2_lt),
    .clock(clock_1_out), .Sa(main_1_sa), .Sb(main_1_sb), .Sc(main_1_sc), .La(main_1_la), .Lb(main_1_lb),
    .Shift(main_1_shift), .Lcount(main_1_lcount), .Sr1(main_1_sr1), .Sr2(main_1_sr2), .Scr(main_1_scr),
    .Cr(main_1_cr), .state(state));
  datapath_main main_2 (
    .Multiplicand(multiplicand), .Sr1(main_1_sr1), .Sb(main_1_sb), .La(main_1_la), .Sr2(main_1_sr2),
    .Sa(main_1_sa), .Multiplier(multiplier), .Lb(main_1_lb), .Cr(main_1_cr), .Scr(main_1_scr),
    .Lcount(main_1_lcount), .clock(clock_1_out), .Sc(main_1_sc), .Shift(main_1_shift), .Hi(Hi), .Lo(Lo),
    .eq1(main_2_eq1), .eq0(main_2_eq0), .eq(main_2_eq), .lt(main_2_lt));
endmodule
