// Logisim project final_controlunit2.circ as structural Verilog: 1 circuit, main circuit main
module main (
  input  start,
  input  restart,
  input  lt,
  input  lt2,
  input  eq,
  input  eq2,
  input  char_found,
  input  select,
  input  clk,
  output Lf,
  output Lm,
  output Sf,
  output Sm,
  output win,
  output lose,
  output [2:0] state,
  output Lt_2,
  output [3:0] user_score,
  output [3:0] machine_score
);

  wire and_1_out, and_2_out, and_3_out, and_4_out, and_5_out, and_6_out, and_7_out, and_8_out, and_9_out,
       and_10_out, and_11_out, and_12_out, and_13_out, and_14_out, and_15_out, and_16_out, and_17_out,
       and_24_out, and_27_out, not_1_out, not_2_out, not_3_out, not_4_out, not_5_out, not_6_out, not_7_out,
       not_8_out, not_9_out, not_10_out, not_11_out, not_12_out, not_13_out, not_14_out, not_15_out,
       not_16_out, not_17_out, not_18_out, not_19_out, not_20_out, not_21_out, not_22_out, not_23_out,
       not_24_out, not_25_out, not_26_out, not_27_out, not_28_out, or_1_out, or_2_out, or_3_out, or_4_out,
       or_5_out, xor_1_out, xor_2_out, xor_3_out;
  wire [1:0] and_23_out, and_26_out, register_2_q, register_3_q;
  wire [2:0] or_7_out;

  Register #(.width(3)) register_1 (.D(or_7_out), .en(1'b1), .Q(state), .clk(clk));  // open: clr
  not not_1 (not_1_out, char_found);
  and and_1 (and_1_out, lt, lt2, not_1_out);
  and and_2 (and_2_out, lt2, eq);
  and and_3 (and_3_out, lt, eq2);
  not not_2 (not_2_out, state[0]);
  not not_3 (not_3_out, state[2]);
  or or_1 (or_1_out, and_1_out, and_2_out, and_3_out);
  not not_4 (not_4_out, restart);
  not not_5 (not_5_out, state[2]);
  not not_6 (not_6_out, state[2]);
  not not_7 (not_7_out, state[0]);
  not not_8 (not_8_out, select);
  xor xor_1 (xor_1_out, state[0], state[1]);
  and and_4 (and_4_out, not_5_out, state[0]);
  and and_5 (and_5_out, lt, lt2, char_found, select);
  and and_6 (and_6_out, lt, select, eq2);
  not not_9 (not_9_out, state[0]);
  not not_10 (not_10_out, state[1]);
  not not_11 (not_11_out, state[1]);
  not not_12 (not_12_out, state[2]);
  not not_13 (not_13_out, state[0]);
  not not_14 (not_14_out, restart);
  not not_15 (not_15_out, state[2]);
  not not_16 (not_16_out, state[0]);
  and and_7 (and_7_out, state[2], not_4_out, xor_1_out);
  and and_8 (and_8_out, state[1], not_17_out);
  not not_17 (not_17_out, restart);
  and and_9 (and_9_out, not_12_out, not_13_out, start);
  and and_10 (and_10_out, state[2], state[0], not_14_out);
  and and_11 (and_11_out, lt, char_found);
  and and_12 (and_12_out, or_1_out, not_2_out, state[1], not_3_out, select);
  or or_2 (or_2_out, not_8_out, and_5_out, and_6_out);
  or or_3 (or_3_out, not_10_out, and_8_out);
  or or_4 (or_4_out, and_9_out, and_10_out);
  or or_5 (or_5_out, and_11_out, eq);
  not not_18 (not_18_out, state[2]);
  not not_19 (not_19_out, state[1]);
  not not_20 (not_20_out, state[2]);
  not not_21 (not_21_out, state[1]);
  not not_22 (not_22_out, state[0]);
  not not_23 (not_23_out, state[1]);
  not not_24 (not_24_out, state[0]);
  and and_13 (and_13_out, not_6_out, state[1], not_7_out, or_2_out);
  and and_14 (and_14_out, state[2], not_9_out, or_3_out);
  and and_15 (and_15_out, not_11_out, or_4_out);
  and and_16 (and_16_out, not_15_out, state[1], not_16_out, lt2, select, or_5_out);
  and and_17 (and_17_out, not_18_out, not_19_out, state[0]);
  and and_18 (Lt_2, not_20_out, state[1], state[0]);
  and and_19 (Sm, state[2], not_21_out, not_22_out);
  and and_20 (win, state[2], not_23_out, state[0]);
  and and_21 (lose, state[2], state[1], not_24_out);
  or or_6 (or_7_out[2], and_12_out, and_7_out);
  or or_7 (or_7_out[0], and_15_out, and_16_out);
  or or_8 (or_7_out[1], and_4_out, and_13_out, and_14_out);
  or or_9 (Lf, and_17_out, Lt_2);
  or or_10 (Lm, and_17_out, Sm);
  Register #(.width(2)) register_2 (.D(and_23_out), .en(1'b1), .Q(register_2_q), .clk(clk));  // open: clr
  Register #(.width(2)) register_3 (.D(and_26_out), .en(1'b1), .Q(register_3_q), .clk(clk));  // open: clr
  xor xor_2 (xor_2_out, register_2_q[1], register_2_q[0]);
  not not_25 (not_25_out, register_2_q[1]);
  not not_26 (not_26_out, register_2_q[0]);
  xor xor_3 (xor_3_out, register_3_q[1], register_3_q[0]);
  not not_27 (not_27_out, register_3_q[1]);
  not not_28 (not_28_out, register_3_q[0]);
  and and_22 (and_23_out[1], win, xor_2_out);
  and and_23 (and_23_out[0], win, not_25_out, not_26_out);
  and and_24 (and_24_out, not_25_out, register_2_q[0]);
  and and_25 (and_26_out[1], lose, xor_3_out);
  and and_26 (and_26_out[0], lose, not_27_out, not_28_out);
  and and_27 (and_27_out, not_27_out, register_3_q[0]);
  Counter #(.width(4), .max('hf)) counter_1 (
    .count(and_24_out), .Q(user_score), .clk(clk));  // open: load, D, carry, clr
  Counter #(.width(4), .max('hf)) counter_2 (
    .count(and_27_out), .Q(machine_score), .clk(clk));  // open: load, D, carry, clr

  assign Sf = Lt_2;
endmodule
