// Logisim project final_datapath.circ as structural Verilog: 1 circuit, main circuit main
module main (
  input  [6:0] in_1,
  input  [6:0] in_2,
  input  [6:0] in_3,
  input  [6:0] in_4,
  input  [6:0] in_5,
  input  [6:0] in_6,
  input  [6:0] in_7,
  input  [6:0] in_8,
  input  clk,
  input  [6:0] Select_char,
  input  selected,
  input  Lf,
  input  Sf,
  input  Lm,
  input  Sm,
  output [3:0] out_16,
  output char_found,
  output select,
  output eq,
  output lt,
  output eq2,
  output lt2,
  output [7:0] led,
  output [6:0] char
);

  wire comparator_1_eq, comparator_2_eq, comparator_3_eq, comparator_4_eq, comparator_5_eq, comparator_6_eq,
       comparator_7_eq, comparator_8_eq, comparator_9_eq, comparator_10_eq, comparator_11_eq,
       comparator_12_eq, comparator_13_eq, comparator_14_eq, comparator_15_eq, comparator_16_eq,
       comparator_17_eq, not_1_out, not_2_out, not_3_out, not_4_out, not_5_out, not_6_out, not_7_out,
       not_8_out, not_9_out, or_1_out;
  wire [3:0] adder_1_out, adder_3_out, adder_4_out, adder_5_out, adder_6_out, adder_7_out, adder_8_out,
       bit_extender_1_out, bit_extender_2_out, bit_extender_3_out, bit_extender_4_out, bit_extender_5_out,
       bit_extender_6_out, bit_extender_7_out, bit_extender_8_out, found_q, multiplexer_1_out;
  wire [7:0] adder_2_out, multiplexer_2_out;

  Multiplexer #(.width(4), .enable("false")) multiplexer_1 (
    .in0(4'b0000), .in1(adder_1_out), .out(multiplexer_1_out), .sel(Sf));
  Multiplexer #(.width(8), .enable("false")) multiplexer_2 (
    .in0({8{1'b0}}), .in1(adder_2_out), .out(multiplexer_2_out), .sel(Sm));
  Register #(.width(4)) found (.D(multiplexer_1_out), .en(Lf), .Q(found_q), .clk(clk));  // open: clr
  Register miss (.D(multiplexer_2_out), .en(Lm), .Q(led), .clk(clk));  // open: clr
  Comparator #(.width(7)) comparator_1 (.a(in_1), .b({7{1'b0}}), .eq(comparator_1_eq));  // open: gt, lt
  Comparator #(.width(7)) comparator_2 (.a(in_2), .b({7{1'b0}}), .eq(comparator_2_eq));  // open: gt, lt
  Comparator #(.width(7)) comparator_3 (.a(in_3), .b({7{1'b0}}), .eq(comparator_3_eq));  // open: gt, lt
  Comparator #(.width(7)) comparator_4 (.a(in_4), .b({7{1'b0}}), .eq(comparator_4_eq));  // open: gt, lt
  Comparator #(.width(7)) comparator_5 (.a(in_5), .b({7{1'b0}}), .eq(comparator_5_eq));  // open: gt, lt
  Comparator #(.width(7)) comparator_6 (.a(in_6), .b({7{1'b0}}), .eq(comparator_6_eq));  // open: gt, lt
  Comparator #(.width(7)) comparator_7 (.a(in_7), .b({7{1'b0}}), .eq(comparator_7_eq));  // open: gt, lt
  Comparator #(.width(7)) comparator_8 (.a(in_8), .b({7{1'b0}}), .eq(comparator_8_eq));  // open: gt, lt
  Comparator #(.width(7)) comparator_9 (.a(Select_char), .b({7{1'b0}}), .eq(comparator_9_eq));  // open: gt, lt
  Adder #(.width(4)) adder_1 (.a(found_q), .b(4'b0001), .out(adder_1_out), .cin(1'b0));  // open: cout
  Adder adder_2 (.a(led), .b(8'h1), .out(adder_2_out), .cin(1'b0));  // open: cout
  not not_1 (not_1_out, comparator_1_eq);
  not not_2 (not_2_out, comparator_2_eq);
  not not_3 (not_3_out, comparator_3_eq);
  not not_4 (not_4_out, comparator_4_eq);
  not not_5 (not_5_out, comparator_5_eq);
  not not_6 (not_6_out, comparator_6_eq);
  not not_7 (not_7_out, comparator_7_eq);
  not not_8 (not_8_out, comparator_8_eq);
  not not_9 (not_9_out, comparator_9_eq);
  Comparator #(.width(7)) comparator_10 (.a(in_8), .b(Select_char), .eq(comparator_10_eq));  // open: gt, lt
  Comparator #(.width(7)) comparator_11 (.a(in_7), .b(Select_char), .eq(comparator_11_eq));  // open: gt, lt
  Comparator #(.width(7)) comparator_12 (.a(in_6), .b(Select_char), .eq(comparator_12_eq));  // open: gt, lt
  Comparator #(.width(7)) comparator_13 (.a(in_1), .b(Select_char), .eq(comparator_13_eq));  // open: gt, lt
  Comparator #(.width(7)) comparator_14 (.a(in_2), .b(Select_char), .eq(comparator_14_eq));  // open: gt, lt
  Comparator #(.width(7)) comparator_15 (.a(in_3), .b(Select_char), .eq(comparator_15_eq));  // open: gt, lt
  Comparator #(.width(7)) comparator_16 (.a(in_4), .b(Select_char), .eq(comparator_16_eq));  // open: gt, lt
  Comparator #(.width(7)) comparator_17 (.a(in_5), .b(Select_char), .eq(comparator_17_eq));  // open: gt, lt
  assign bit_extender_1_out = {{3{1'b0}}, not_1_out};  // Bit_Extender bit_extender_1
  assign bit_extender_2_out = {{3{1'b0}}, not_2_out};  // Bit_Extender bit_extender_2
  assign bit_extender_3_out = {{3{1'b0}}, not_3_out};  // Bit_Extender bit_extender_3
  assign bit_extender_4_out = {{3{1'b0}}, not_4_out};  // Bit_Extender bit_extender_4
  assign bit_extender_5_out = {{3{1'b0}}, not_5_out};  // Bit_Extender bit_extender_5
  assign bit_extender_6_out = {{3{1'b0}}, not_6_out};  // Bit_Extender bit_extender_6
  assign bit_extender_7_out = {{3{1'b0}}, not_7_out};  // Bit_Extender bit_extender_7
  assign bit_extender_8_out = {{3{1'b0}}, not_8_out};  // Bit_Extender bit_extender_8
  Comparator comparator_18 (.a(led), .b(8'ha), .eq(eq2), .lt(lt2));  // open: gt
  or or_1 (or_1_out, comparator_10_eq, comparator_11_eq, comparator_12_eq, comparator_13_eq, comparator_14_eq, comparator_15_eq, comparator_16_eq, comparator_17_eq);
  Comparator #(.width(4)) comparator_19 (.a(found_q), .b(out_16), .eq(eq), .lt(lt));  // open: gt
  and and_1 (select, selected, 1'b1);
  and and_2 (char_found, or_1_out, not_9_out, selected);
  Adder #(.width(4)) adder_3 (.a(bit_extender_1_out), .b(bit_extender_2_out), .out(adder_3_out));  // open: cin, cout
  Adder #(.width(4)) adder_4 (.a(bit_extender_3_out), .b(bit_extender_4_out), .out(adder_4_out));  // open: cin, cout
  Adder #(.width(4)) adder_5 (.a(bit_extender_5_out), .b(bit_extender_6_out), .out(adder_5_out));  // open: cin, cout
  Adder #(.width(4)) adder_6 (.a(bit_extender_7_out), .b(bit_extender_8_out), .out(adder_6_out));  // open: cin, cout
  Adder #(.width(4)) adder_7 (.a(adder_3_out), .b(adder_4_out), .out(adder_7_out));  // open: cin, cout
  Adder #(.width(4)) adder_8 (.a(adder_5_out), .b(adder_6_out), .out(adder_8_out));  // open: cin, cout
  Adder #(.width(4)) adder_9 (.a(adder_7_out), .b(adder_8_out), .out(out_16));  // open: cin, cout

  assign char = Select_char;
endmodule
