// Logisim project final_led.circ as structural Verilog: 1 circuit, main circuit main
module main (
  input  a,
  input  b,
  input  c,
  input  d,
  input  [7:0] in_5,
  output led1,
  output led2,
  output led3,
  output led4,
  output led5,
  output led6,
  output led7,
  output led8,
  output led9,
  output led10
);

  wire and_1_out, and_2_out, and_3_out, and_4_out, and_5_out, and_6_out, and_7_out;

  or or_1 (led1, in_5[0], in_5[1], in_5[2], in_5[3]);
  or or_2 (led2, in_5[1], in_5[2], in_5[3]);
  and and_1 (and_1_out, in_5[1], in_5[0]);
  or or_3 (led4, in_5[2], in_5[3]);
  and and_2 (and_2_out, in_5[2], in_5[0]);
  and and_3 (and_3_out, in_5[2], in_5[1]);
  and and_4 (and_4_out, in_5[2], in_5[1]);
  and and_5 (and_5_out, in_5[2], in_5[1], in_5[0]);
  and and_6 (and_6_out, in_5[3], in_5[0]);
  and and_7 (and_7_out, in_5[3], in_5[1]);
  and and_8 (led10, in_5[3], in_5[1]);
  or or_4 (led3, and_1_out, in_5[2], in_5[3]);
  or or_5 (led5, and_2_out, and_3_out, in_5[3]);
  or or_6 (led6, and_4_out, in_5[3]);
  or or_7 (led7, and_5_out, in_5[3]);
  or or_8 (led9, and_6_out, and_7_out);

  assign led8 = in_5[3];
endmodule
