// Logisim project final_project2.circ as structural Verilog: 1 circuit, main circuit main
module main (
  input  [6:0] in_1,
  input  [6:0] in_2,
  input  [6:0] in_3,
  input  [6:0] in_4,
  input  [6:0] in_5,
  input  [6:0] in_6,
  input  [6:0] in_7,
  input  [6:0] in_8,
  input  [6:0] select_char,
  output win,
  output lose,
  output [2:0] state
);

  wire clock_1_out, main_1_char_found, main_1_eq, main_1_eq2, main_1_lt, main_1_lt2, main_1_select,
       main_2_lf, main_2_lm, main_2_lt_2, main_2_sf, main_2_sm, main_3_a, main_3_b_2, main_3_c_2, main_3_d_2,
       main_3_e, main_3_f, main_3_g, main_4_led1, main_4_led2, main_4_led3, main_4_led4, main_4_led5,
       main_4_led6, main_4_led7, main_4_led8, main_4_led9, main_4_led10, main_5_a, main_5_b_2, main_5_c_2,
       main_5_d_2, main_5_e, main_5_f, main_5_g, main_6_a, main_6_b_2, main_6_c_2, main_6_d_2, main_6_e,
       main_6_f, main_6_g, restart_out, selected_out, start_out;
  wire [3:0] main_1_out_16, main_2_machine_score, main_2_user_score;
  wire [6:0] main_1_char;
  wire [7:0] main_1_led;

  Clock clock_1 (.out(clock_1_out));
  Button selected (.out(selected_out));
  Button start (.out(start_out));
  Button restart (.out(restart_out));
  final_datapath_main main_1 (
    .in_1(in_1), .in_2(in_2), .in_3(in_3), .in_4(in_4), .in_5(in_5), .in_6(in_6), .in_7(in_7), .in_8(in_8),
    .clk(clock_1_out), .Select_char(select_char), .selected(selected_out), .Lf(main_2_lf), .Sf(main_2_sf),
    .Lm(main_2_lm), .Sm(main_2_sm), .out_16(main_1_out_16), .char_found(main_1_char_found),
    .select(main_1_select), .eq(main_1_eq), .lt(main_1_lt), .eq2(main_1_eq2), .lt2(main_1_lt2),
    .led(main_1_led), .char(main_1_char));
  final_controlunit2_main main_2 (
    .start(start_out), .restart(restart_out), .lt(main_1_lt), .lt2(main_1_lt2), .eq(main_1_eq),
    .eq2(main_1_eq2), .char_found(main_1_char_found), .select(main_1_select), .clk(clock_1_out),
    .Lf(main_2_lf), .Lm(main_2_lm), .Sf(main_2_sf), .Sm(main_2_sm), .win(win), .lose(lose), .state(state),
    .Lt_2(main_2_lt_2), .user_score(main_2_user_score), .machine_score(main_2_machine_score));
  final_7_seg_main main_3 (
    .in_1(main_1_out_16), .a(main_3_a), .b_2(main_3_b_2), .c_2(main_3_c_2), .d_2(main_3_d_2), .e(main_3_e),
    .f(main_3_f), .g(main_3_g));  // open: D, C, B, A_2
  final_led_main main_4 (
    .in_5(main_1_led), .led1(main_4_led1), .led2(main_4_led2), .led3(main_4_led3), .led4(main_4_led4),
    .led5(main_4_led5), .led6(main_4_led6), .led7(main_4_led7), .led8(main_4_led8), .led9(main_4_led9),
    .led10(main_4_led10));  // open: a, b, c, d
  _7_Segment_Display u_7_segment_display_1 (
    .g(main_3_g), .f(main_3_f), .a(main_3_a), .b(main_3_b_2), .e(main_3_e), .d(main_3_d_2), .c(main_3_c_2));  // open: dp
  LED led_1 (.in(main_4_led1));
  LED led_2 (.in(main_4_led2));
  LED led_3 (.in(main_4_led3));
  LED led_4 (.in(main_4_led4));
  LED led_5 (.in(main_4_led5));
  LED led_6 (.in(main_4_led6));
  LED led_7 (.in(main_4_led7));
  LED led_8 (.in(main_4_led8));
  LED led_9 (.in(main_4_led9));
  LED led_10 (.in(main_4_led10));
  TTY tty_1 (.data(main_1_char), .clk(clock_1_out), .we(main_2_lt_2), .clr(restart_out));
  final_7_seg_main main_5 (
    .in_1(main_2_user_score), .a(main_5_a), .b_2(main_5_b_2), .c_2(main_5_c_2), .d_2(main_5_d_2),
    .e(main_5_e), .f(main_5_f), .g(main_5_g));  // open: D, C, B, A_2
  final_7_seg_main main_6 (
    .in_1(main_2_machine_score), .a(main_6_a), .b_2(main_6_b_2), .c_2(main_6_c_2), .d_2(main_6_d_2),
    .e(main_6_e), .f(main_6_f), .g(main_6_g));  // open: D, C, B, A_2
  _7_Segment_Display u_7_segment_display_2 (
    .g(main_5_g), .f(main_5_f), .a(main_5_a), .b(main_5_b_2), .e(main_5_e), .d(main_5_d_2), .c(main_5_c_2));  // open: dp
  _7_Segment_Display u_7_segment_display_3 (
    .g(main_6_g), .f(main_6_f), .a(main_6_a), .b(main_6_b_2), .e(main_6_e), .d(main_6_d_2), .c(main_6_c_2));  // open: dp

  // Notes on the sheet:
  //   char1
  //   char2
  //   char3
  //   char4
  //   char5
  //   char6
  //   char7
  //   char8
  //   word_char_num
  //   User_Score
  //   Machine_Score
endmodule
