// Logisim project LedGame.circ as structural Verilog: 1 circuit, main circuit main
module main (
);

  wire and_3_out, and_6_out, and_9_out, and_10_out, and_11_out, and_12_out, and_13_out, and_14_out,
       and_15_out, and_16_out, and_17_out, and_18_out, and_19_out, and_20_out, and_21_out, and_22_out,
       and_23_out, and_24_out, and_25_out, and_26_out, and_27_out, and_28_out, and_29_out, and_30_out,
       and_31_out, and_32_out, and_33_out, and_34_out, and_35_out, and_38_out, clock_1_out, clock_2_out,
       clock_3_out, clock_4_out, clock_5_out, clock_6_out, clock_7_out, not_1_out, not_2_out, not_3_out,
       not_4_out, not_5_out, not_6_out, not_7_out, not_8_out, not_9_out, not_10_out, not_11_out, not_12_out,
       not_13_out, not_14_out, not_15_out, not_16_out, not_17_out, not_18_out, not_19_out, not_20_out,
       not_21_out, not_22_out, not_23_out, not_24_out, not_25_out, not_26_out, not_27_out, not_28_out,
       not_29_out, not_30_out, not_31_out, not_32_out, not_33_out, not_34_out, not_35_out, not_36_out,
       not_37_out, not_38_out, not_39_out, not_40_out, not_41_out, not_42_out, not_43_out, not_44_out,
       not_45_out, not_46_out, not_47_out, not_48_out, not_49_out, not_50_out, not_51_out, not_52_out,
       not_53_out, not_54_out, Player1_out, Player2_out, R_out, xor_1_out, xor_2_out, xor_3_out, xor_4_out;
  wire [1:0] and_2_out, and_5_out, and_8_out, and_37_out, register_1_q, register_2_q, register_3_q,
       register_5_q;
  wire [2:0] or_3_out, register_4_q;
  wire [7:0] counter_1_q, counter_2_q;

  Clock clock_1 (.out(clock_1_out));
  Button Player1 (.out(Player1_out));
  Clock clock_2 (.out(clock_2_out));
  Button Player2 (.out(Player2_out));
  Clock clock_3 (.out(clock_3_out));
  Register #(.width(2)) register_1 (.D(and_2_out), .en(1'b1), .Q(register_1_q), .clk(clock_1_out));  // open: clr
  Register #(.width(2)) register_2 (.D(and_5_out), .en(1'b1), .Q(register_2_q), .clk(clock_2_out));  // open: clr
  Register #(.width(2)) register_3 (.D(and_8_out), .en(1'b1), .Q(register_3_q), .clk(clock_3_out));  // open: clr
  Clock clock_4 (.out(clock_4_out));
  xor xor_1 (xor_1_out, register_1_q[1], register_1_q[0]);
  not not_1 (not_1_out, register_1_q[1]);
  not not_2 (not_2_out, register_1_q[0]);
  xor xor_2 (xor_2_out, register_2_q[1], register_2_q[0]);
  not not_3 (not_3_out, register_2_q[1]);
  not not_4 (not_4_out, register_2_q[0]);
  xor xor_3 (xor_3_out, register_3_q[1], register_3_q[0]);
  not not_5 (not_5_out, register_3_q[1]);
  not not_6 (not_6_out, register_3_q[0]);
  Register #(.width(3)) register_4 (.D(or_3_out), .en(1'b1), .Q(register_4_q), .clk(clock_4_out));  // open: clr
  and and_1 (and_2_out[1], and_10_out, xor_1_out);
  and and_2 (and_2_out[0], and_10_out, not_1_out, not_2_out);
  and and_3 (and_3_out, not_1_out, register_1_q[0]);
  and and_4 (and_5_out[1], Player1_out, xor_2_out);
  and and_5 (and_5_out[0], Player1_out, not_3_out, not_4_out);
  and and_6 (and_6_out, not_3_out, register_2_q[0]);
  and and_7 (and_8_out[1], Player2_out, xor_3_out);
  and and_8 (and_8_out[0], Player2_out, not_5_out, not_6_out);
  and and_9 (and_9_out, not_5_out, register_3_q[0]);
  and and_10 (and_10_out, register_4_q[2], register_4_q[1], not_7_out);
  not not_7 (not_7_out, register_4_q[0]);
  Button R (.out(R_out));
  Clock clock_5 (.out(clock_5_out));
  and and_11 (and_11_out, not_8_out, register_4_q[1], register_4_q[0]);
  not not_8 (not_8_out, register_4_q[2]);
  Register #(.width(2)) register_5 (.D(and_37_out), .en(1'b1), .Q(register_5_q), .clk(clock_5_out));  // open: clr
  and and_12 (and_12_out, register_4_q[2], register_4_q[1]);
  and and_13 (and_13_out, register_4_q[2], register_4_q[0]);
  not not_9 (not_9_out, register_4_q[1]);
  and and_14 (and_14_out, register_4_q[2], not_9_out, not_10_out);
  not not_10 (not_10_out, register_4_q[0]);
  not not_11 (not_11_out, register_4_q[2]);
  and and_15 (and_15_out, not_11_out, not_12_out, not_13_out);
  not not_12 (not_12_out, register_4_q[1]);
  not not_13 (not_13_out, register_4_q[0]);
  not not_14 (not_14_out, register_4_q[2]);
  and and_16 (and_16_out, not_14_out, not_15_out, register_4_q[0]);
  not not_15 (not_15_out, register_4_q[1]);
  not not_16 (not_16_out, register_4_q[2]);
  and and_17 (and_17_out, not_16_out, register_4_q[1], not_17_out);
  not not_17 (not_17_out, register_4_q[0]);
  and and_18 (and_18_out, register_4_q[1], register_4_q[0]);
  not not_18 (not_18_out, register_4_q[1]);
  not not_19 (not_19_out, register_4_q[0]);
  not not_20 (not_20_out, and_9_out);
  not not_21 (not_21_out, R_out);
  not not_22 (not_22_out, and_9_out);
  not not_23 (not_23_out, R_out);
  not not_24 (not_24_out, R_out);
  not not_25 (not_25_out, R_out);
  not not_26 (not_26_out, R_out);
  not not_27 (not_27_out, register_4_q[2]);
  not not_28 (not_28_out, and_6_out);
  not not_29 (not_29_out, R_out);
  not not_30 (not_30_out, and_6_out);
  not not_31 (not_31_out, R_out);
  not not_32 (not_32_out, R_out);
  not not_33 (not_33_out, R_out);
  not not_34 (not_34_out, and_9_out);
  not not_35 (not_35_out, R_out);
  not not_36 (not_36_out, R_out);
  not not_37 (not_37_out, register_4_q[2]);
  not not_38 (not_38_out, register_4_q[0]);
  not not_39 (not_39_out, and_6_out);
  not not_40 (not_40_out, R_out);
  not not_41 (not_41_out, and_6_out);
  not not_42 (not_42_out, and_9_out);
  not not_43 (not_43_out, R_out);
  not not_44 (not_44_out, R_out);
  not not_45 (not_45_out, register_4_q[2]);
  not not_46 (not_46_out, and_9_out);
  not not_47 (not_47_out, R_out);
  not not_48 (not_48_out, R_out);
  not not_49 (not_49_out, register_4_q[1]);
  not not_50 (not_50_out, register_4_q[0]);
  not not_51 (not_51_out, and_9_out);
  not not_52 (not_52_out, R_out);
  Clock clock_6 (.out(clock_6_out));
  Clock clock_7 (.out(clock_7_out));
  LED led_1 (.in(and_13_out));
  LED led_2 (.in(and_12_out));
  and and_19 (and_19_out, not_18_out, not_19_out, and_6_out, not_20_out, not_21_out);
  and and_20 (and_20_out, register_4_q[2], not_22_out, not_23_out);
  and and_21 (and_21_out, register_4_q[2], and_6_out, not_24_out);
  and and_22 (and_22_out, register_4_q[2], register_4_q[0], not_25_out);
  and and_23 (and_23_out, register_4_q[2], register_4_q[1], not_26_out);
  and and_24 (and_24_out, not_27_out, register_4_q[0], not_28_out, and_9_out, not_29_out);
  and and_25 (and_25_out, register_4_q[1], not_30_out, not_31_out);
  and and_26 (and_26_out, register_4_q[1], and_9_out, not_32_out);
  and and_27 (and_27_out, register_4_q[1], register_4_q[0], not_33_out);
  and and_28 (and_28_out, register_4_q[2], register_4_q[0], and_6_out, not_34_out, not_35_out);
  and and_29 (and_29_out, register_4_q[2], register_4_q[1], not_36_out);
  and and_30 (and_30_out, not_37_out, not_38_out, not_39_out, and_9_out, not_40_out);
  and and_31 (and_31_out, register_4_q[0], not_41_out, not_42_out, not_43_out);
  and and_32 (and_32_out, register_4_q[0], and_6_out, and_9_out, not_44_out);
  and and_33 (and_33_out, not_45_out, register_4_q[1], and_6_out, not_46_out, not_47_out);
  and and_34 (and_34_out, register_4_q[1], register_4_q[0], not_48_out);
  and and_35 (and_35_out, register_4_q[2], not_49_out, not_50_out, and_6_out, not_51_out, not_52_out);
  xor xor_4 (xor_4_out, register_5_q[1], register_5_q[0]);
  not not_53 (not_53_out, register_5_q[1]);
  not not_54 (not_54_out, register_5_q[0]);
  Counter counter_1 (.count(and_3_out), .Q(counter_1_q), .clk(clock_6_out));  // open: load, D, carry, clr
  Counter counter_2 (.count(and_38_out), .Q(counter_2_q), .clk(clock_7_out));  // open: load, D, carry, clr
  LED led_3 (.in(and_14_out));
  or or_1 (or_3_out[2], and_19_out, and_20_out, and_21_out, and_22_out, and_23_out);
  or or_2 (or_3_out[1], and_24_out, and_25_out, and_26_out, and_27_out, and_28_out, and_29_out);
  or or_3 (or_3_out[0], and_30_out, and_31_out, and_32_out, and_33_out, and_34_out, and_35_out);
  and and_36 (and_37_out[1], and_11_out, xor_4_out);
  and and_37 (and_37_out[0], and_11_out, not_53_out, not_54_out);
  and and_38 (and_38_out, not_53_out, register_5_q[0]);
  // Probe on counter_1_q
  // Probe on counter_2_q
  LED led_4 (.in(and_16_out));
  LED led_5 (.in(and_15_out));
  LED led_6 (.in(and_17_out));
  LED led_7 (.in(and_18_out));

  // Notes on the sheet:
  //   S1
  //   S0
  //   S1
  //   S0
  //   S1
  //   S0
  //   N1
  //   N0
  //   N1
  //   N0
  //   N1
  //   N0
  //   S2
  //   S1
  //   S0
  //   bo1
  //   bo2
  //   Reset
  //   S1
  //   S0
  //   N2
  //   N1
  //   N0
  //   N1
  //   N0
endmodule
