// Logisim project controlunit.circ as structural Verilog: 1 circuit, main circuit main
module main (
  input  gt,
  input  eq,
  input  lt,
  input  start,
  input  CLK,
  output Lm,
  output La,
  output Lb,
  output Sm,
  output Sa,
  output Sr,
  output [2:0] STATE
);

  wire and_1_out, and_3_out, and_4_out, and_5_out, and_6_out, and_7_out, and_8_out, and_9_out, and_12_out,
       not_1_out, not_2_out, not_3_out, or_1_out, or_2_out, or_4_out, xor_1_out;
  wire [2:0] or_5_out;

  Register #(.width(3)) u_STATE (.D(or_5_out), .en(1'b1), .Q(STATE), .clk(CLK));  // open: clr
  or or_1 (or_1_out, gt, eq);
  not not_1 (not_1_out, STATE[0]);
  not not_2 (not_2_out, STATE[1]);
  not not_3 (not_3_out, STATE[2]);
  xor xor_1 (xor_1_out, STATE[1], STATE[0]);
  and and_1 (and_1_out, STATE[0], eq);
  and and_2 (or_5_out[2], or_1_out, STATE[0], STATE[1], not_3_out);
  and and_3 (and_3_out, not_3_out, xor_1_out);
  and and_4 (and_4_out, STATE[2], not_2_out, not_1_out);
  and and_5 (and_5_out, not_3_out, start);
  or or_2 (or_2_out, not_1_out, and_1_out);
  or or_3 (or_5_out[1], and_3_out, and_4_out);
  or or_4 (or_4_out, and_5_out, STATE[2]);
  and and_6 (and_6_out, not_2_out, not_1_out, or_4_out);
  and and_7 (and_7_out, not_3_out, STATE[1], or_2_out);
  and and_8 (and_8_out, not_1_out, not_2_out, not_3_out);
  and and_9 (and_9_out, STATE[0], not_2_out, not_3_out);
  and and_10 (Lb, not_1_out, STATE[1], not_3_out);
  and and_11 (Sa, STATE[2], not_1_out, not_2_out);
  and and_12 (and_12_out, STATE[2], STATE[0], not_2_out);
  or or_5 (or_5_out[0], and_6_out, and_7_out);
  or or_6 (Lm, and_9_out, Sa);
  or or_7 (La, Lb, Sa);
  or or_8 (Sr, and_8_out, and_12_out);

  assign Sm = Sa;

  // Notes on the sheet:
  //   S0
  //   S1
  //   S2
  //   S4
  //   S5
endmodule
