// Logisim project multiplication.circ as structural Verilog: 1 circuit, main circuit main
module main (
  input  [15:0] a_i,
  input  [15:0] b_i,
  output [15:0] res,
  output [2:0] STATE
);

  wire CLK_out, main_1_la, main_1_lb, main_1_lm, main_1_sa, main_1_sm, main_1_sr, main_2_eq, main_2_gt,
       main_2_lt, start_out;

  Button start (.out(start_out));
  Clock CLK (.out(CLK_out));
  controlunit_main main_1 (
    .gt(main_2_gt), .eq(main_2_eq), .lt(main_2_lt), .start(start_out), .CLK(CLK_out), .Lm(main_1_lm),
    .La(main_1_la), .Lb(main_1_lb), .Sm(main_1_sm), .Sa(main_1_sa), .Sr(main_1_sr), .STATE(STATE));
  datapath_main main_2 (
    .Sa(main_1_sa), .a_i(a_i), .La(main_1_la), .b_i(b_i), .Lb(main_1_lb), .Lm(main_1_lm), .Sm(main_1_sm),
    .Sr(main_1_sr), .CLK(CLK_out), .gt(main_2_gt), .eq(main_2_eq), .lt(main_2_lt), .res(res));
endmodule
